// Logisim project FullAdder.circ as structural Verilog: 1 circuit, main circuit nand0
module nand0 (
  input  A,
  input  B,
  output Y
);

  wire transistor_4_out;

  Transistor transistor_1 (.in(1'b1), .out(Y), .gate(B));
  Transistor transistor_2 (.in(1'b1), .out(Y), .gate(A));
  Transistor #(.\type ("n")) transistor_3 (.in(transistor_4_out), .out(Y), .gate(A));
  Transistor #(.\type ("n")) transistor_4 (.in(1'b0), .out(transistor_4_out), .gate(B));

  // Notes on the sheet:
  //   CMOS implementation of a NAND gate
endmodule
